# Fritzing sketch PuzzleCircuit (saved by Fritzing 0.4.2b)
breadboards: 1

parts:
  Arduino1 = Arduino
  R1 = Resistor [resistance=10k package=THT]
  R1_2 = Resistor [resistance=10k package=THT]
  R1_3 = Resistor [resistance=10k package=THT]
  R1_4 = Resistor [resistance=10k package=THT]
  S1 = Pushbutton [package=THT]
  S1_2 = Pushbutton [package=THT]
  S1_3 = Pushbutton [package=THT]
  S1_4 = Pushbutton [package=THT]
  LED1 = Red LED - 5mm
  LED2 = Blue LED - 5mm
  LED3 = green LED - 5mm
  LED4 = white LED - 5mm

nets:
  N1: Arduino1.GND, R1.Pin_1, R1_2.Pin_1, LED1.cathode, LED2.cathode
  N2: Arduino1.D11, LED4.anode
  N3: Arduino1.D10, LED3.anode
  N4: Arduino1.D9, LED2.anode
  N5: Arduino1.D8, LED1.anode
  N6: Arduino1.D4, R1_4.Pin_0, S1_4.leg0
  N7: Arduino1.D3, R1_3.Pin_0, S1_3.leg0
  N8: Arduino1.D2, R1_2.Pin_0, S1_2.leg0
  N9: Arduino1.D1TX, R1.Pin_0, S1.leg0
  N10: Arduino1.+5V, R1_3.Pin_1, R1_4.Pin_1, S1.leg1, S1_2.leg1, S1_3.leg1, S1_4.leg1, LED3.cathode, LED4.cathode

notes:
  White - LED Outpu
  Gray - Switch Input
